// Logisim project 3bit 2 input.circ as structural Verilog: 1 circuit, main circuit main
module main (
  input  A0,
  input  B0,
  input  A1,
  input  B1,
  input  A2,
  input  B2,
  output out_7,
  output out_8,
  output out_9,
  output out_10
);

  wire and_1_out, and_2_out, and_3_out, and_4_out, and_5_out, and_6_out, or_1_out, or_2_out, xor_1_out,
       xor_2_out, xor_3_out;

  xor xor_1 (xor_1_out, A0, B0);
  xor xor_2 (xor_2_out, A1, B1);
  xor xor_3 (xor_3_out, A2, B2);
  xor xor_4 (out_7, xor_1_out, 1'b0);
  and and_1 (and_1_out, 1'b0, xor_1_out);
  and and_2 (and_2_out, A0, B0);
  xor xor_5 (out_8, xor_2_out, or_1_out);
  and and_3 (and_3_out, or_1_out, xor_2_out);
  and and_4 (and_4_out, A1, B1);
  xor xor_6 (out_9, xor_3_out, or_2_out);
  and and_5 (and_5_out, or_2_out, xor_3_out);
  and and_6 (and_6_out, A2, B2);
  or or_1 (or_1_out, and_1_out, and_2_out);
  or or_2 (or_2_out, and_3_out, and_4_out);
  or or_3 (out_10, and_5_out, and_6_out);

  // Notes on the sheet:
  //   C0 IN
  //   S0
  //   C0 O
  //   S0
  //   S1
  //   S2
  //   C OUT
endmodule
