// Logisim project Circuit without using NAND gate.circ as structural Verilog: 1 circuit, main circuit main
module main (
  input  A,
  input  B,
  input  C,
  input  D,
  input  E
);

  wire and_1_out, and_2_out, and_3_out, and_4_out, not_1_out, not_2_out, not_3_out, not_4_out, not_5_out,
       or_1_out;

  not not_1 (not_1_out, A);
  not not_2 (not_2_out, B);
  not not_3 (not_3_out, C);
  not not_4 (not_4_out, D);
  not not_5 (not_5_out, E);
  and and_1 (and_1_out, not_1_out, not_2_out, C, D, not_5_out);
  and and_2 (and_2_out, B, C, not_4_out, not_5_out);
  and and_3 (and_3_out, A, not_3_out, D, not_5_out);
  and and_4 (and_4_out, A, B, not_5_out);
  or or_1 (or_1_out, and_1_out, and_2_out, and_3_out, and_4_out);
  LED led_1 (.in(or_1_out));

  // Notes on the sheet:
  //   Circuit without using NAND gate
endmodule
