// Logisim project Critical_Nand.circ as structural Verilog: 1 circuit, main circuit main
module main (
  input  [4:0] in_1
);

  wire nand_1_out, nand_2_out, nand_3_out, nand_4_out, nand_5_out, nand_6_out, nand_7_out, nand_8_out,
       nand_9_out, nand_10_out, nand_11_out, nand_12_out, nand_13_out, nand_14_out, nand_15_out, nand_16_out,
       nand_17_out, nand_18_out, nand_19_out, nand_20_out, nand_21_out, nand_22_out, nand_23_out, nand_24_out;

  nand nand_1 (nand_1_out, in_1[4], in_1[4]);
  nand nand_2 (nand_2_out, in_1[2], in_1[2]);
  nand nand_3 (nand_3_out, in_1[3], in_1[3]);
  nand nand_4 (nand_4_out, in_1[0], in_1[0]);
  nand nand_5 (nand_5_out, in_1[1], in_1[1]);
  nand nand_6 (nand_6_out, in_1[4], nand_2_out);
  nand nand_7 (nand_7_out, nand_1_out, in_1[2]);
  nand nand_8 (nand_8_out, nand_3_out, in_1[1]);
  nand nand_9 (nand_9_out, in_1[3], nand_5_out);
  nand nand_10 (nand_10_out, nand_6_out, nand_6_out);
  nand nand_11 (nand_11_out, nand_7_out, nand_7_out);
  nand nand_12 (nand_12_out, nand_8_out, nand_8_out);
  nand nand_13 (nand_13_out, nand_9_out, nand_9_out);
  nand nand_14 (nand_14_out, nand_10_out, nand_13_out);
  nand nand_15 (nand_15_out, nand_11_out, nand_12_out);
  nand nand_16 (nand_16_out, nand_12_out, nand_10_out);
  nand nand_17 (nand_17_out, nand_13_out, nand_11_out);
  nand nand_18 (nand_18_out, nand_14_out, nand_15_out);
  nand nand_19 (nand_19_out, nand_16_out, nand_17_out);
  nand nand_20 (nand_20_out, nand_18_out, nand_18_out);
  nand nand_21 (nand_21_out, nand_20_out, nand_22_out);
  nand nand_22 (nand_22_out, nand_19_out, nand_19_out);
  nand nand_23 (nand_23_out, nand_21_out, nand_4_out);
  LED led_1 (.in(nand_24_out));
  nand nand_24 (nand_24_out, nand_23_out, nand_23_out);
endmodule
