// Logisim project Seven Segment Display.circ as structural Verilog: 1 circuit, main circuit main
module main (
  input  in_1,
  input  in_2,
  input  in_3,
  input  D
);

  wire A_out, and_1_out, and_2_out, and_3_out, and_4_out, and_5_out, and_6_out, and_7_out, and_8_out,
       and_9_out, and_10_out, and_11_out, and_12_out, and_13_out, and_14_out, and_15_out, and_16_out, B_out,
       C_out, D_out, E_out, F_out, G_out, not_1_out, not_2_out, not_3_out, not_4_out, undriven, undriven_2,
       undriven_3, undriven_4;

  not not_1 (not_1_out, in_1);
  not not_2 (not_2_out, in_2);
  not not_3 (not_3_out, in_3);
  not not_4 (not_4_out, D);
  and and_1 (and_1_out, not_1_out, undriven_3);
  and and_2 (and_2_out, undriven, undriven, not_2_out, not_3_out);
  and and_3 (and_3_out, not_1_out, not_3_out, not_4_out);
  and and_4 (and_4_out, not_1_out, undriven_2, undriven_2);
  and and_5 (and_5_out, not_1_out, not_2_out, not_3_out);
  and and_6 (and_6_out, undriven, not_2_out, not_3_out);
  and and_7 (and_7_out, not_1_out, not_2_out, undriven_3);
  and and_8 (and_8_out, not_1_out, undriven_4, undriven_2, not_3_out);
  and and_9 (and_9_out, not_1_out, undriven_2, not_3_out);
  and and_10 (and_10_out, not_1_out, undriven_2, undriven_4);
  and and_11 (and_11_out, not_2_out, not_3_out, not_4_out);
  and and_12 (and_12_out, not_1_out, not_2_out);
  and and_13 (and_13_out, not_1_out, undriven_3, undriven_4);
  and and_14 (and_14_out, not_1_out, not_1_out, undriven_4);
  and and_15 (and_15_out, not_1_out, undriven_3, not_4_out);
  and and_16 (and_16_out, not_1_out, undriven_2, not_4_out);
  or u_D (D_out, and_11_out, and_6_out, and_7_out, and_15_out, and_8_out);
  or F (F_out, and_6_out, and_3_out, and_9_out, and_16_out);
  or A (A_out, and_1_out, and_10_out, and_2_out, and_11_out);
  or B (B_out, and_12_out, and_3_out, and_13_out);
  or C (C_out, and_4_out, and_14_out, and_5_out, and_6_out);
  or E (E_out, and_11_out, and_15_out);
  or G (G_out, and_7_out, and_6_out, and_9_out, and_15_out);
  _7_Segment_Display u_7_segment_display_1 (.a(A_out), .e(D_out), .c(E_out));  // open: g, f, b, d, dp

  // Notes on the sheet:
  //   A
  //   B
  //   C
endmodule
